# Fritzing sketch Tez Devre Fritzing (saved by Fritzing 0.9.3b)
breadboards: 2

parts:
  Parça1 = Arduino Mega 2560 (Rev3)
  YwRobot_Power_Supply1 = YwRobot Breadboard Power Supply [part_number=545043]
  Parça2 = RFID-RC522-v2
  Parça3 = RFID-RC522-v2
  Parça4 = RFID-RC522-v2
  Parça5 = RFID-RC522-v2
  J2 = Basic Servo
  hc-sr1 = hc-sr04
  LED1 = smd LED [color="Red (633nm)" package="0805 [SMD]"]
  LED2 = smd LED [color="Red (633nm)" package="0805 [SMD]"]
  LED3 = smd LED [color="Red (633nm)" package="0805 [SMD]"]
  LED4 = smd LED [color="Red (633nm)" package="0805 [SMD]"]
  LED5 = smd LED [color="Green (565nm)" package="0805 [SMD]"]
  LED6 = smd LED [color="Green (565nm)" package="0805 [SMD]"]
  LED7 = smd LED [color="Green (565nm)" package="0805 [SMD]"]
  LED8 = smd LED [color="Green (565nm)" package="0805 [SMD]"]
  LED9 = smd LED [color="Blue (430nm)" package="0805 [SMD]"]
  LED10 = smd LED [color="Blue (430nm)" package="0805 [SMD]"]
  LED11 = smd LED [color="Blue (430nm)" package="0805 [SMD]"]
  LED12 = smd LED [color="Blue (430nm)" package="0805 [SMD]"]

nets:
  N1: Parça1.D3_PWM, J2.pulse
  N2: Parça1.D5_PWM, Parça2.RST, Parça3.RST, Parça4.RST, Parça5.RST
  N3: Parça1.D22, LED1.anode
  N4: Parça1.D24, LED4.anode
  N5: Parça1.D26, LED3.anode
  N6: Parça1.D28, LED2.anode
  N7: Parça1.D30, LED8.anode
  N8: Parça1.D31, Parça2.SDA
  N9: Parça1.D32, LED7.anode
  3.3V: Parça1.D33, YwRobot_Power_Supply1.VCC#5, Parça2.3.3V, Parça3.3.3V, Parça4.3.3V, Parça5.3.3V
  N10: Parça1.D35, Parça3.SDA
  N11: Parça1.D36, LED6.anode
  N12: Parça1.D37, Parça4.SDA
  N13: Parça1.D38, LED12.anode
  N14: Parça1.D40, LED11.anode
  N15: Parça1.D42, LED9.anode
  N16: Parça1.D44, LED10.anode
  VCC: Parça1.D46, YwRobot_Power_Supply1.VCC#9, J2.vcc, hc-sr1.VCC, hc-sr1.Trig
  N17: Parça1.D47, hc-sr1.Echo
  N18: Parça1.D50, Parça2.MISO, Parça3.MISO, Parça4.MISO, Parça5.MISO
  N19: Parça1.D51, Parça2.MOSI, Parça3.MOSI, Parça4.MOSI, Parça5.MOSI
  N20: Parça1.D52, Parça2.SCK, Parça3.SCK, Parça4.SCK, Parça5.SCK
  GND: YwRobot_Power_Supply1.GND#11, Parça2.GND, Parça3.GND, Parça4.GND, Parça5.GND, LED1.cathode, LED4.cathode, LED7.cathode, LED8.cathode, LED11.cathode, LED12.cathode
  GND_2: YwRobot_Power_Supply1.GND#13, J2.gnd, hc-sr1.GND, LED2.cathode, LED3.cathode, LED5.cathode, LED6.cathode, LED9.cathode, LED10.cathode

notes:
  PWM
  5(KAHVERENGİ KABLO=ARDUINO MEGA RESET PİNİ)
  3(SARI KABLO= SERVO DATA PİN)
  DIGITAL PORT
  22(KIRMIZI KABLO = KIRMIZI LED RFID1)
  24(KIRMIZI KABLO = KIRMIZI LED RFID2)
  26(KIRMIZI KABLO = KIRMIZI LED RFID3)
  28(KIRMIZI KABLO = KIRMIZI LED RFID4)
  30(YEŞİL KABLO = YEŞİL LED RFID1)
  32(YEŞİL KABLO = YEŞİL LED RFID2)
  34(YEŞİL KABLO = YEŞİL LED RFID3)
  36(YEŞİL KABLO = YEŞİL LED RFID4)
  38(MAVİ KABLO = MAVİ LED RFID1)
  40(MAVİ KABLO = MAVİ LED RFID2)
  42(MAVİ KABLO = MAVİ LED RFID3)
  44(MAVİ KABLO = MAVİ LED RFID4)
  46(GRİ KABLO= HC-SR04 TRIG PİN)
  47(SİYAH KABLO= HC-SR04 ECHO PİN)
  SPI HABERLEŞME PORTLARI (DIGITAL BÖLÜMDE)
  31,33,35,37(TURKUAZ KABLO = RFID SDA(SS) PİNLERİ SIRASIYLA
  (SS_1_PIN 31
  SS_2_PIN 33
  SS_3_PIN 35
  SS_4_PIN 37))
  50 (YEŞİL KABLO = SPI MISO)
  51 (SARI KABLO = SPI MOSI)
  52 (PEMBE KABLO = SPI SCK)

custom parts:
  YwRobot Breadboard Power Supply: The YwRobot Breadboard Power Supply (MB-V2) has two power rails; they can be 5V or 3V3. Power to the module can be provided through the female USB socket or through the A10 (female) 2.1mm power jack.
  RFID-RC522-v2: A simple China made RFID-RC522 Reader; do check the pin labels, as this is a MFRC522 based clone.
